// Logisim project 1.circ as structural Verilog
// q
module main (
  input  R,
  input  S,
  input  R2,
  input  S2,
  output Q,
  output Q_not,
  output Q2,
  output Q2_not
);

  nor nor_1 (Q, R, Q_not);
  nor nor_2 (Q_not, Q, S);
  rs_latch rs_latch_1 (.s(R2), .r(S2), .q(Q2), .q_not(Q2_not));
endmodule

// VHDL entity rs_latch, as the project stores it:
LIBRARY ieee;
USE ieee.std_logic_1164.ALL;

ENTITY rs_latch IS
    PORT (
        s     : IN std_logic;
        r     : IN std_logic;
        q     : OUT std_logic;
        q_not : OUT std_logic
    );
END rs_latch;

ARCHITECTURE dataflow OF rs_latch IS
    SIGNAL q_internal     : std_logic;
    SIGNAL q_not_internal : std_logic;
BEGIN
    q_internal     <= r NOR q_not_internal;
    q_not_internal <= s NOR q_internal;
    
    q       <= q_internal;
    q_not   <= q_not_internal;
END dataflow;
