// Logisim project 2.circ as structural Verilog
module main (
  input  D,
  input  en,
  input  en2,
  input  D2,
  output Q,
  output Q_not,
  output Q2,
  output Q2_not
);

  wire nand_1_out, nand_2_out, not_1_out;

  not not_1 (not_1_out, D);
  nand nand_1 (nand_1_out, D, en);
  nand nand_2 (nand_2_out, not_1_out, en);
  nand nand_3 (Q, nand_1_out, Q_not);
  nand nand_4 (Q_not, Q, nand_2_out);
  d_latch d_latch_1 (.en(en2), .d(D2), .q(Q2), .q_not(Q2_not));
endmodule

// VHDL entity d_latch, as the project stores it:
LIBRARY ieee;
USE ieee.std_logic_1164.ALL;

ENTITY d_latch IS
    PORT (
        en    : IN std_logic;
        d     : IN std_logic;
        q     : OUT std_logic;
        q_not : OUT std_logic
    );
END d_latch;

ARCHITECTURE behavior OF d_latch IS
BEGIN
    process(en, d)
    begin
        -- Enable이 1일 때만 D 값을 출력으로 전달 (Follow)
        if (en = '1') then
            q <= d;
            q_not <= not d;
        end if;
        -- Enable이 0일 때는 아무 동작도 하지 않음 (자동으로 이전 값 Hold)
    end process;
END behavior;
