// Logisim project 3.circ as structural Verilog
module main (
  input  D,
  input  clk,
  input  clk2,
  input  D2,
  output Q,
  output Q_not,
  output Q2,
  output Q2_not
);

  wire nand_1_out, nand_2_out, nand_3_out, nand_4_out, nand_5_out, nand_6_out, not_1_out, not_2_out,
       not_3_out, not_4_out;

  not not_1 (not_1_out, D);
  not not_2 (not_2_out, clk);
  nand nand_1 (nand_1_out, D, not_2_out);
  nand nand_2 (nand_2_out, not_1_out, not_2_out);
  nand nand_3 (nand_3_out, nand_1_out, nand_4_out);
  nand nand_4 (nand_4_out, nand_3_out, nand_2_out);
  not not_3 (not_3_out, nand_3_out);
  not not_4 (not_4_out, not_2_out);
  d_flipflop d_flipflop_1 (.clk(clk2), .d(D2), .q(Q2), .q_not(Q2_not));
  nand nand_5 (nand_5_out, nand_3_out, not_4_out);
  nand nand_6 (nand_6_out, not_3_out, not_4_out);
  nand nand_7 (Q, nand_5_out, Q_not);
  nand nand_8 (Q_not, Q, nand_6_out);
endmodule

// VHDL entity d_flipflop, as the project stores it:
LIBRARY ieee;
USE ieee.std_logic_1164.ALL;

ENTITY d_flipflop IS
    PORT (
        clk   : IN  std_logic;
        d     : IN  std_logic;
        q     : OUT std_logic;
        q_not : OUT std_logic
    );
END d_flipflop;

ARCHITECTURE behavior OF d_flipflop IS
BEGIN
    process(clk)
    begin
        if rising_edge(clk) then
            q     <= d;
            q_not <= not d;
        end if;
    end process;
END behavior;
