// Logisim project 5.circ as structural Verilog
module main (
  input  D,
  input  clk,
  input  clr,
  input  set,
  input  in_5,
  input  in_6,
  input  in_7,
  input  in_8,
  output Q,
  output Q_not,
  output out_11,
  output out_12
);

  wire nand_1_out, nand_2_out, nand_3_out, nand_4_out, nand_5_out, nand_6_out, nand_7_out, not_1_out,
       not_2_out, not_3_out, not_4_out, not_5_out;

  not not_1 (not_1_out, clr);
  not not_2 (not_2_out, D);
  not not_3 (not_3_out, clk);
  nand nand_1 (nand_1_out, D, not_3_out);
  nand nand_2 (nand_2_out, not_2_out, not_3_out);
  nand nand_3 (nand_3_out, not_1_out, set);
  nand nand_4 (nand_4_out, nand_1_out, nand_3_out, nand_5_out);
  nand nand_5 (nand_5_out, nand_4_out, not_1_out, nand_2_out);
  not not_4 (not_4_out, nand_4_out);
  not not_5 (not_5_out, not_3_out);
  nand nand_6 (nand_6_out, nand_4_out, not_5_out);
  nand nand_7 (nand_7_out, not_4_out, not_5_out);
  dff_ms dff_ms_1 (.clk(in_5), .d(in_6), .set(in_7), .clr(in_8), .q(out_11), .q_not(out_12));
  nand nand_8 (Q, nand_6_out, nand_3_out, Q_not);
  nand nand_9 (Q_not, Q, not_1_out, nand_7_out);
endmodule

// VHDL entity dff_ms, as the project stores it:
LIBRARY ieee;
USE ieee.std_logic_1164.ALL;

ENTITY dff_ms IS
    PORT (
        clk   : IN  std_logic;
        d     : IN  std_logic;
        set   : IN  std_logic;
        clr   : IN  std_logic;
        q     : OUT std_logic;
        q_not : OUT std_logic
    );
END dff_ms;

ARCHITECTURE behavior OF dff_ms IS
    SIGNAL q_int : std_logic := '0';
BEGIN
    PROCESS(clk, clr, set)
    BEGIN
        IF clr = '1' THEN
            q_int <= '0';
        ELSIF set = '1' THEN
            q_int <= '1';
        ELSIF rising_edge(clk) THEN
            q_int <= d;
        END IF;
    END PROCESS;

    q     <= q_int;
    q_not <= NOT q_int;
END behavior;
